// Logisim project ai.circ as structural Verilog: 2 circuits, main circuit AI
module AI (
  input  reset,
  input  [7:0] x,
  input  [7:0] y,
  output [7:0] batY
);

  wire _0xf1_out, _0xf2_out, _0xf3_out, cdm_8_mark5_1_p1, cdm_8_mark5_1_p2, cdm_8_mark5_1_p4,
       cdm_8_mark5_1_p5, cdm_8_mark5_1_p6, cdm_8_mark5_1_p7, cdm_8_mark5_1_p8, cdm_8_mark5_1_p9,
       cdm_8_mark5_1_p10, clock, code, data, decoder_1_out1, decoder_1_out2, decoder_1_out3, I_Osel,
       nand_1_out, nand_2_out, not_1_out, not_2_out, RAM, rd_wr;
  wire [3:0] I_Oadr;
  wire [7:0] cdm_8_mark5_1_p13, cdm_8_mark5_1_p14, I_Odata;
  wire [7:4] cdm_8_mark5_1_p12;

  and and_1 (I_Osel, not_1_out, clock, data);
  Decoder #(.select(4)) decoder_1 (
    .out1(decoder_1_out1), .out2(decoder_1_out2), .out3(decoder_1_out3), .sel(I_Oadr));  // open: out0, out4, out5, out6, out7, out8, out9, out10, out11, out12, out13, out14, out15, en
  // Probe on cdm_8_mark5_1_p5
  // Probe on cdm_8_mark5_1_p4
  // Probe on cdm_8_mark5_1_p2
  // Probe on cdm_8_mark5_1_p1
  Clock clock_1 (.out(clock));
  not not_1 (not_1_out, nand_1_out);
  and and_2 (RAM, nand_1_out, data);
  // Probe on cdm_8_mark5_1_p7
  // Probe on cdm_8_mark5_1_p6
  // Probe on cdm_8_mark5_1_p8
  // CdM_8_mark5 cdm_8_mark5_1: pin names not known; wires that end beside it: cdm_8_mark5_1_p1, cdm_8_mark5_1_p2, clock, cdm_8_mark5_1_p4, cdm_8_mark5_1_p5, cdm_8_mark5_1_p6, cdm_8_mark5_1_p7, cdm_8_mark5_1_p8, cdm_8_mark5_1_p9, cdm_8_mark5_1_p10, rd_wr, {cdm_8_mark5_1_p12, I_Oadr}, cdm_8_mark5_1_p13, cdm_8_mark5_1_p14
  nand nand_1 (nand_1_out, cdm_8_mark5_1_p12[4], cdm_8_mark5_1_p12[5], cdm_8_mark5_1_p12[6], cdm_8_mark5_1_p12[7]);
  Decoder decoder_2 (.out0(code), .out1(data), .sel(cdm_8_mark5_1_p9), .en(cdm_8_mark5_1_p10));
  assign I_Odata = not_2_out ? cdm_8_mark5_1_p13 : 8'bz;  // Controlled_Buffer controlled_buffer_1
  not not_2 (not_2_out, rd_wr);
  assign cdm_8_mark5_1_p14 = rd_wr ? I_Odata : 8'bz;  // Controlled_Buffer controlled_buffer_2
  and _0xf1 (_0xf1_out, decoder_1_out1, ~rd_wr, I_Osel);  // AND_Gate
  and _0xf2 (_0xf2_out, decoder_1_out2, rd_wr, I_Osel);
  and _0xf3 (_0xf3_out, decoder_1_out3, rd_wr, I_Osel);
  and and_3 (RAM, data, nand_2_out);
  nand nand_2 (nand_2_out, _0xf1_out, _0xf2_out, _0xf3_out);
  Register register_1 (.D(I_Odata), .Q(batY), .clk(_0xf1_out));  // open: en, clr
  assign I_Odata = _0xf2_out ? x : 8'bz;  // Controlled_Buffer controlled_buffer_3
  assign I_Odata = _0xf3_out ? y : 8'bz;  // Controlled_Buffer controlled_buffer_4
  bat_fault bat_fault_1 (.batY_beg(batY), .upd(_0xf1_out));  // open: batY_end
  ROM rom_1 (.addr({cdm_8_mark5_1_p12, I_Oadr}), .data(I_Odata), .sel(code));
  RAM #(.bus("separate")) ram_1 (
    .addr({cdm_8_mark5_1_p12, I_Oadr}), .din(I_Odata), .data(I_Odata), .sel(RAM), .clk(clock), .ld(rd_wr),
    .clr(reset));  // open: str

  // Notes on the sheet:
  //   contents of rom_1 (hex, n*v repeats v):
  //   cd f0 d1 f2 d2 f3 b5 ba 7 5*9b f e0 32 b 5*9b f e0 29 d0 1d 34 84 98 d3 1f 12 7e ea 27 3b 1e ee 32
  //   d0 1d 34 84 98 78 ea 32 32 d0 f1 a2 ee 2 d4
endmodule

module bat_fault (
  input  upd,
  input  [7:0] batY_beg,
  output [7:0] batY_end
);

  wire random_3_out;
  wire [7:0] adder_1_out, divider_1_out, divider_2_out, random_1_out, random_2_out, subtractor_1_out;

  Random random_1 (.clk(upd), .next(1'b1), .out(random_1_out));  // open: clr
  Random random_2 (.clk(upd), .next(1'b1), .out(random_2_out));  // open: clr
  Divider divider_1 (.a(random_1_out), .b(8'h10), .out(divider_1_out));  // open: upper, rem
  Divider divider_2 (.a(random_2_out), .b(8'h10), .out(divider_2_out));  // open: upper, rem
  // Probe on divider_1_out
  Adder adder_1 (.a(divider_1_out), .b(batY_beg), .out(adder_1_out));  // open: cin, cout
  Subtractor subtractor_1 (.a(batY_beg), .b(divider_2_out), .out(subtractor_1_out));  // open: bin, bout
  // Probe on divider_2_out
  Random #(.width(1)) random_3 (.clk(upd), .next(1'b1), .out(random_3_out));  // open: clr
  // Probe on adder_1_out
  // Probe on subtractor_1_out
  Multiplexer #(.width(8)) multiplexer_1 (
    .in0(adder_1_out), .in1(subtractor_1_out), .out(batY_end), .sel(random_3_out));  // open: en
  // Probe on batY_end
endmodule
