// Logisim project klava.circ as structural Verilog: 3 circuits, main circuit row_main
module row_main (
  input  [4:0] ROW,
  input  [4:0] ballX,
  input  [4:0] ballY,
  input  [4:0] leftbatY,
  input  [4:0] rightbatY,
  output [4:0] NEXT_ROW,
  output [4:0] out_7,
  output [4:0] out_8,
  output [4:0] out_9,
  output [4:0] out_10,
  output [31:0] out_11
);

  wire comparator_1_eq, comparator_2_eq, comparator_3_eq, xor_1_out;
  wire [4:0] mux;
  wire [31:0] decoder_1_out0, decoder_2_out30;

  Adder #(.width(5)) adder_1 (.a(5'b00001), .b(ROW), .out(NEXT_ROW));  // open: cin, cout
  Comparator #(.width(5)) comparator_1 (.a(ROW), .b(ballX), .eq(comparator_1_eq));  // open: gt, lt
  Comparator #(.width(5)) comparator_2 (.a(ROW), .b(5'b00010), .eq(comparator_2_eq));  // open: gt, lt
  Comparator #(.width(5)) comparator_3 (.a(ROW), .b(5'b11101), .eq(comparator_3_eq));  // open: gt, lt
  Multiplexer #(.width(5)) multiplexer_1 (
    .in0(leftbatY), .in1(rightbatY), .out(mux), .sel(comparator_3_eq), .en(xor_1_out));
  xor xor_1 (xor_1_out, comparator_2_eq, comparator_3_eq);
  Decoder #(.select(5)) decoder_1 (
    .out0(decoder_1_out0[0]), .out1(decoder_1_out0[1]), .out2(decoder_1_out0[2]), .out3(decoder_1_out0[3]),
    .out4(decoder_1_out0[4]), .out5(decoder_1_out0[5]), .out6(decoder_1_out0[6]), .out7(decoder_1_out0[7]),
    .out8(decoder_1_out0[8]), .out9(decoder_1_out0[9]), .out10(decoder_1_out0[10]),
    .out11(decoder_1_out0[11]), .out12(decoder_1_out0[12]), .out13(decoder_1_out0[13]),
    .out14(decoder_1_out0[14]), .out15(decoder_1_out0[15]), .out16(decoder_1_out0[16]),
    .out17(decoder_1_out0[17]), .out18(decoder_1_out0[18]), .out19(decoder_1_out0[19]),
    .out20(decoder_1_out0[20]), .out21(decoder_1_out0[21]), .out22(decoder_1_out0[22]),
    .out23(decoder_1_out0[23]), .out24(decoder_1_out0[24]), .out25(decoder_1_out0[25]),
    .out26(decoder_1_out0[26]), .out27(decoder_1_out0[27]), .out28(decoder_1_out0[28]),
    .out29(decoder_1_out0[29]), .out30(decoder_1_out0[30]), .out31(decoder_1_out0[31]), .sel(ballY),
    .en(comparator_1_eq));
  Decoder #(.select(5)) decoder_2 (
    .out0(decoder_2_out30[0]), .out1(decoder_2_out30[1]), .out2(decoder_2_out30[2]),
    .out3(decoder_2_out30[3]), .out4(decoder_2_out30[4]), .out5(decoder_2_out30[5]),
    .out6(decoder_2_out30[6]), .out7(decoder_2_out30[7]), .out8(decoder_2_out30[8]),
    .out9(decoder_2_out30[9]), .out10(decoder_2_out30[10]), .out11(decoder_2_out30[11]),
    .out12(decoder_2_out30[12]), .out13(decoder_2_out30[13]), .out14(decoder_2_out30[14]),
    .out15(decoder_2_out30[15]), .out16(decoder_2_out30[16]), .out17(decoder_2_out30[17]),
    .out18(decoder_2_out30[18]), .out19(decoder_2_out30[19]), .out20(decoder_2_out30[20]),
    .out21(decoder_2_out30[21]), .out22(decoder_2_out30[22]), .out23(decoder_2_out30[23]),
    .out24(decoder_2_out30[24]), .out25(decoder_2_out30[25]), .out26(decoder_2_out30[26]),
    .out27(decoder_2_out30[27]), .out28(decoder_2_out30[28]), .out29(decoder_2_out30[29]),
    .out30(decoder_2_out30[30]), .out31(decoder_2_out30[31]), .sel(mux), .en(xor_1_out));
  Pull_Resistor pull_resistor_1 (.node(decoder_1_out0));
  Pull_Resistor pull_resistor_2 (.node(decoder_2_out30));
  assign out_11 = decoder_1_out0 | decoder_2_out30 | {decoder_2_out30[30:0], 1'b0} | {decoder_2_out30[29:0], 2'b00};  // OR_Gate or_1, 32 bits wide

  assign out_7 = ballX;
  assign out_8 = ballY;
  assign out_9 = leftbatY;
  assign out_10 = rightbatY;
endmodule

module _8rows (
  input  [4:0] in_1,
  input  [4:0] in_2,
  input  [4:0] in_3,
  input  [4:0] in_4,
  input  [4:0] in_5,
  output [31:0] out_6,
  output [31:0] out_7,
  output [31:0] out_8,
  output [31:0] out_9,
  output [31:0] out_10,
  output [31:0] out_11,
  output [31:0] out_12,
  output [31:0] out_13,
  output [4:0] out_14,
  output [4:0] out_15,
  output [4:0] out_16,
  output [4:0] out_17,
  output [4:0] out_18
);

  wire [4:0] row_main_1_next_row, row_main_1_out_7, row_main_1_out_8, row_main_1_out_9, row_main_1_out_10,
       row_main_2_next_row, row_main_2_out_7, row_main_2_out_8, row_main_2_out_9, row_main_2_out_10,
       row_main_3_next_row, row_main_3_out_7, row_main_3_out_8, row_main_3_out_9, row_main_3_out_10,
       row_main_4_next_row, row_main_4_out_7, row_main_4_out_8, row_main_4_out_9, row_main_4_out_10,
       row_main_5_next_row, row_main_5_out_7, row_main_5_out_8, row_main_5_out_9, row_main_5_out_10,
       row_main_6_next_row, row_main_6_out_7, row_main_6_out_8, row_main_6_out_9, row_main_6_out_10,
       row_main_7_next_row, row_main_7_out_7, row_main_7_out_8, row_main_7_out_9, row_main_7_out_10;

  row_main row_main_1 (
    .ROW(in_1), .ballX(in_2), .out_7(row_main_1_out_7), .ballY(in_3), .out_8(row_main_1_out_8),
    .leftbatY(in_4), .out_9(row_main_1_out_9), .rightbatY(in_5), .out_10(row_main_1_out_10),
    .NEXT_ROW(row_main_1_next_row), .out_11(out_6));
  row_main row_main_2 (
    .ROW(row_main_1_next_row), .ballX(row_main_1_out_7), .out_7(row_main_2_out_7), .ballY(row_main_1_out_8),
    .out_8(row_main_2_out_8), .leftbatY(row_main_1_out_9), .out_9(row_main_2_out_9),
    .rightbatY(row_main_1_out_10), .out_10(row_main_2_out_10), .NEXT_ROW(row_main_2_next_row), .out_11(out_7));
  row_main row_main_3 (
    .ROW(row_main_2_next_row), .ballX(row_main_2_out_7), .out_7(row_main_3_out_7), .ballY(row_main_2_out_8),
    .out_8(row_main_3_out_8), .leftbatY(row_main_2_out_9), .out_9(row_main_3_out_9),
    .rightbatY(row_main_2_out_10), .out_10(row_main_3_out_10), .NEXT_ROW(row_main_3_next_row), .out_11(out_8));
  row_main row_main_4 (
    .ROW(row_main_3_next_row), .ballX(row_main_3_out_7), .out_7(row_main_4_out_7), .ballY(row_main_3_out_8),
    .out_8(row_main_4_out_8), .leftbatY(row_main_3_out_9), .out_9(row_main_4_out_9),
    .rightbatY(row_main_3_out_10), .out_10(row_main_4_out_10), .NEXT_ROW(row_main_4_next_row), .out_11(out_9));
  row_main row_main_5 (
    .ROW(row_main_4_next_row), .ballX(row_main_4_out_7), .out_7(row_main_5_out_7), .ballY(row_main_4_out_8),
    .out_8(row_main_5_out_8), .leftbatY(row_main_4_out_9), .out_9(row_main_5_out_9),
    .rightbatY(row_main_4_out_10), .out_10(row_main_5_out_10), .NEXT_ROW(row_main_5_next_row), .out_11(out_10));
  row_main row_main_6 (
    .ROW(row_main_5_next_row), .ballX(row_main_5_out_7), .out_7(row_main_6_out_7), .ballY(row_main_5_out_8),
    .out_8(row_main_6_out_8), .leftbatY(row_main_5_out_9), .out_9(row_main_6_out_9),
    .rightbatY(row_main_5_out_10), .out_10(row_main_6_out_10), .NEXT_ROW(row_main_6_next_row), .out_11(out_11));
  row_main row_main_7 (
    .ROW(row_main_6_next_row), .ballX(row_main_6_out_7), .out_7(row_main_7_out_7), .ballY(row_main_6_out_8),
    .out_8(row_main_7_out_8), .leftbatY(row_main_6_out_9), .out_9(row_main_7_out_9),
    .rightbatY(row_main_6_out_10), .out_10(row_main_7_out_10), .NEXT_ROW(row_main_7_next_row), .out_11(out_12));
  row_main row_main_8 (
    .ROW(row_main_7_next_row), .ballX(row_main_7_out_7), .out_7(out_15), .ballY(row_main_7_out_8),
    .out_8(out_16), .leftbatY(row_main_7_out_9), .out_9(out_17), .rightbatY(row_main_7_out_10),
    .out_10(out_18), .NEXT_ROW(out_14), .out_11(out_13));
endmodule

module keyboard (
  input  [6:0] keyb,
  output [1:0] dir
);

  wire comparator_1_eq, comparator_2_eq, comparator_3_eq, comparator_4_eq;

  Comparator #(.width(7)) comparator_1 (.a(keyb), .b(7'b1110111), .eq(comparator_1_eq));  // open: gt, lt
  Comparator #(.width(7)) comparator_2 (.a(keyb), .b(7'b1000110), .eq(comparator_2_eq));  // open: gt, lt
  Comparator #(.width(7)) comparator_3 (.a(keyb), .b(7'b1110011), .eq(comparator_3_eq));  // open: gt, lt
  Comparator #(.width(7)) comparator_4 (.a(keyb), .b(7'b1001011), .eq(comparator_4_eq));  // open: gt, lt
  or or_1 (dir[0], comparator_1_eq, comparator_2_eq);
  or or_2 (dir[1], comparator_3_eq, comparator_4_eq);

  // Notes on the sheet:
  //   ascii w
  //   ascii ц
  //   ascii s
  //   ascii ы
  //   UP
  //   DOWN
endmodule
