// Logisim project processor.circ as structural Verilog: 9 circuits, main circuit main
module main (
  input  AI,
  input  nonstop,
  input  [2:0] in_3,
  input  in_4,
  input  [2:0] screenstate
);

  wire clk, match_out, res;
  wire [1:0] keyboard_3_out_2;
  wire [4:0] control_1_lb, control_1_rb, control_1_x, control_1_y, lstep_1_out_4, register_1_q;
  wire [6:0] keyboard_1_data, keyboard_2_data;
  wire [7:0] Lscore, Rscore;
  wire [31:0] color_1_out_4, screen_1_out_6, screen_1_out_7, screen_1_out_8, screen_1_out_9, screen_1_out_10,
       screen_1_out_11, screen_1_out_12, screen_1_out_13, screen_1_out_14, screen_1_out_15, screen_1_out_16,
       screen_1_out_17, screen_1_out_18, screen_1_out_19, screen_1_out_20, screen_1_out_21, screen_1_out_22,
       screen_1_out_23, screen_1_out_24, screen_1_out_25, screen_1_out_26, screen_1_out_27, screen_1_out_28,
       screen_1_out_29, screen_1_out_30, screen_1_out_31, screen_1_out_32, screen_1_out_33, screen_1_out_34,
       screen_1_out_35, screen_1_out_36, screen_1_out_37;

  Keyboard keyboard_1 (.clk(clk), .data(keyboard_1_data));  // open: re, clr, avail
  Clock clock_1 (.out(clk));
  Button match (.out(match_out));
  Button button_1 (.out(res));
  control control_1 (
    .ctr(match_out), .res(res), .kin(keyboard_1_data), .x(control_1_x), .lb(control_1_lb), .clk(clk),
    .y(control_1_y), .rb(control_1_rb), .enemyscore(Rscore), .myscore(Lscore), .AI(AI), .nonstop(nonstop));
  Keyboard keyboard_2 (.clk(clk), .data(keyboard_2_data));  // open: re, clr, avail
  Hex_Digit_Display hex_digit_display_1 (.value(Lscore[7:4]));  // open: dp
  keyboard keyboard_3 (.in_1(keyboard_2_data), .out_2(keyboard_3_out_2));
  Hex_Digit_Display hex_digit_display_2 (.value(Lscore[3:0]));  // open: dp
  DotMatrix #(.matrixcols(1), .matrixrows(32)) dotmatrix_1 (.col0(color_1_out_4));
  DotMatrix #(.matrixcols(32), .matrixrows(32)) dotmatrix_2 (
    .col0(screen_1_out_35), .col1(screen_1_out_33), .col2(screen_1_out_31), .col3(screen_1_out_29),
    .col4(screen_1_out_27), .col5(screen_1_out_25), .col6(screen_1_out_23), .col7(screen_1_out_6),
    .col8(screen_1_out_7), .col9(screen_1_out_8), .col10(screen_1_out_9), .col11(screen_1_out_10),
    .col12(screen_1_out_11), .col13(screen_1_out_12), .col14(screen_1_out_13), .col15(screen_1_out_14),
    .col16(screen_1_out_15), .col17(screen_1_out_16), .col18(screen_1_out_17), .col19(screen_1_out_18),
    .col20(screen_1_out_19), .col21(screen_1_out_20), .col22(screen_1_out_21), .col23(screen_1_out_22),
    .col24(screen_1_out_24), .col25(screen_1_out_26), .col26(screen_1_out_28), .col27(screen_1_out_30),
    .col28(screen_1_out_32), .col29(screen_1_out_34), .col30(screen_1_out_36), .col31(screen_1_out_37));
  screen screen_1 (
    .ballx(control_1_x), .bally(control_1_y), .left_bat(control_1_lb), .right_bat(control_1_rb),
    .out_35(screen_1_out_35), .out_33(screen_1_out_33), .out_31(screen_1_out_31), .out_29(screen_1_out_29),
    .out_27(screen_1_out_27), .out_25(screen_1_out_25), .out_23(screen_1_out_23), .out_6(screen_1_out_6),
    .out_7(screen_1_out_7), .out_8(screen_1_out_8), .out_9(screen_1_out_9), .out_10(screen_1_out_10),
    .out_11(screen_1_out_11), .out_12(screen_1_out_12), .out_13(screen_1_out_13), .out_14(screen_1_out_14),
    .out_15(screen_1_out_15), .out_16(screen_1_out_16), .out_17(screen_1_out_17), .out_18(screen_1_out_18),
    .out_19(screen_1_out_19), .out_20(screen_1_out_20), .out_21(screen_1_out_21), .out_22(screen_1_out_22),
    .out_24(screen_1_out_24), .out_26(screen_1_out_26), .out_28(screen_1_out_28), .out_30(screen_1_out_30),
    .out_32(screen_1_out_32), .out_34(screen_1_out_34), .out_36(screen_1_out_36), .out_37(screen_1_out_37),
    .state(screenstate));
  Register #(.width(5)) register_1 (.D(lstep_1_out_4), .Q(register_1_q), .clk(clk));  // open: en, clr
  lstep lstep_1 (.clk(clk), .move(keyboard_3_out_2), .rs(res), .out_4(lstep_1_out_4));
  DotMatrix #(.matrixcols(1), .matrixrows(32)) dotmatrix_3 (.col0(color_1_out_4));
  color color_1 (.xball(control_1_y), .mode(in_3), .clk(clk), .out_4(color_1_out_4));
  Hex_Digit_Display hex_digit_display_3 (.value(Rscore[3:0]));  // open: dp
  Hex_Digit_Display hex_digit_display_4 (.value(Rscore[7:4]));  // open: dp

  // Notes on the sheet:
  //   000 - y ball
  //   001 - gravity
  //   010 reverse grav
  //   011 - fire
  //   000 - game
  //   001 - start
endmodule

module control (
  input  AI,
  input  [6:0] kin,
  input  ctr,
  input  res,
  input  nonstop,
  input  clk,
  output [4:0] x,
  output [4:0] lb,
  output [4:0] rb,
  output [7:0] myscore,
  output [4:0] y,
  output [7:0] enemyscore
);

  wire _2clk, _4clk, _8clk, ad, and_1_out, and_2_out, and_3_out, and_4_out, clk_t, clk_t_t,
       clllision_1_out_5, clllision_2_out_5, comparator_1_eq, comparator_2_eq, comparator_3_eq,
       comparator_3_lt, comparator_6_eq, comparator_7_eq, controlled_buffer_1_out, controlled_buffer_15_out,
       controlled_buffer_16_out, d_ff_1_q, d_ff_2_q, d_ff_3_q, da, goal1, goal2, not_1_out, not_2_out,
       not_3_out, not_6_out, not_8_out, not_9_out, not_10_out, not_11_out, not_12_out, or_1_out, or_2_out,
       or_3_out, or_4_out, or_6_out, or_7_out, or_8_out, pull_resistor_2_node, pull_resistor_3_node,
       register_2_q, register_3_q, register_4_q, state, vx, vy, xor_1_out;
  wire [1:0] state_q;
  wire [1:1] keyboard_1_out_2;
  wire [2:0] controlled_buffer_4_out;
  wire [4:0] adder_3_out, adder_4_out, adder_5_out, controlled_buffer_6_out, controlled_buffer_8_out,
       controlled_buffer_10_out, multiplexer_1_out, multiplexer_2_out, register_1_q, rstep_1_out_4;
  wire [7:0] adder_1_out, adder_2_out, ai_1_baty;

  Adder adder_1 (.a(8'h6), .b(myscore), .out(adder_1_out));  // open: cin, cout
  Clock clock_1 (.out(clk_t_t));
  Adder adder_2 (.a(8'h6), .b(enemyscore), .out(adder_2_out));  // open: cin, cout
  Counter counter_1 (
    .load(comparator_2_eq), .D(adder_1_out), .count(goal1), .Q(myscore), .clk(_2clk), .clr(res));  // open: carry
  rstep rstep_1 (.in_1(kin), .clk(clk_t_t), .rs(or_1_out), .out_4(rstep_1_out_4));
  or or_1 (or_1_out, res, ~state);  // OR_Gate
  Counter counter_2 (
    .load(comparator_1_eq), .D(adder_2_out), .count(goal2), .Q(enemyscore), .clk(_2clk), .clr(res));  // open: carry
  not not_1 (not_1_out, nonstop);
  assign controlled_buffer_1_out = not_1_out ? or_2_out : 1'bz;  // Controlled_Buffer controlled_buffer_1
  or or_2 (or_2_out, goal2, goal1);
  Pull_Resistor pull_resistor_1 (.node(controlled_buffer_1_out));
  or or_3 (or_3_out, controlled_buffer_1_out, ctr);
  Comparator #(.width(4)) comparator_1 (.a(enemyscore[3:0]), .b(4'b1010), .eq(comparator_1_eq));  // open: gt, lt
  assign rb = AI ? register_1_q : 5'bz;  // Controlled_Buffer controlled_buffer_2
  not not_2 (not_2_out, AI);
  assign rb = not_2_out ? rstep_1_out_4 : 5'bz;  // Controlled_Buffer controlled_buffer_3
  assign controlled_buffer_4_out = ad ? {1'b1, state_q} : 3'bz;  // Controlled_Buffer controlled_buffer_4
  assign controlled_buffer_4_out = or_3_out ? 3'b000 : 3'bz;  // Controlled_Buffer controlled_buffer_5
  Comparator #(.width(4)) comparator_2 (.a(myscore[3:0]), .b(4'b1010), .eq(comparator_2_eq));  // open: gt, lt
  AI ai_1 (.reset(res), .x({2'b00, vx, x}), .y({2'b00, vy, y}), .batY(ai_1_baty));
  Register #(.width(3)) u_state (
    .D(controlled_buffer_4_out), .Q({state, state_q}), .clk(clk_t_t), .clr(res));  // open: en
  lstep lstep_1 (.clk(clk_t_t), .move({keyboard_1_out_2[1], da}), .rs(or_4_out), .out_4(lb));
  keyboard keyboard_1 (.in_1(kin), .out_2({keyboard_1_out_2[1], da}));
  or or_4 (or_4_out, res, ~state);  // OR_Gate
  or or_5 (ad, keyboard_1_out_2[1], da);
  Comparator #(.width(5), .mode("unsigned")) comparator_3 (
    .a(register_1_q), .b(ai_1_baty[4:0]), .eq(comparator_3_eq), .lt(comparator_3_lt));  // open: gt
  not not_3 (not_3_out, comparator_3_lt);
  assign controlled_buffer_6_out = comparator_3_lt ? 5'b00001 : 5'bz;  // Controlled_Buffer controlled_buffer_6
  assign controlled_buffer_6_out = not_3_out ? {5{1'b1}} : 5'bz;  // Controlled_Buffer controlled_buffer_7
  D_Flip_Flop d_ff_1 (.clk(clk_t_t), .D(_2clk), .Q(d_ff_1_q));  // open: Qn, preset, en, reset
  not not_4 (_2clk, d_ff_1_q);
  Adder #(.width(5)) adder_3 (.a(register_1_q), .b(controlled_buffer_6_out), .out(adder_3_out));  // open: cin, cout
  D_Flip_Flop d_ff_2 (.clk(_2clk), .D(_4clk), .Q(d_ff_2_q));  // open: Qn, preset, en, reset
  not not_5 (_4clk, d_ff_2_q);
  not not_6 (not_6_out, comparator_3_eq);
  Register #(.width(5)) register_1 (.D(adder_3_out), .en(not_6_out), .Q(register_1_q), .clk(clk_t));  // open: clr
  D_Flip_Flop d_ff_3 (.clk(_4clk), .D(_8clk), .Q(d_ff_3_q));  // open: Qn, preset, en, reset
  not not_7 (_8clk, d_ff_3_q);
  Register #(.width(1)) register_2 (.D(goal1), .Q(register_2_q), .clk(clk_t_t), .clr(goal2));  // open: en
  not not_8 (not_8_out, res);
  and and_1 (and_1_out, not_8_out, state);
  xor xor_1 (xor_1_out, vx, or_6_out);
  not not_9 (not_9_out, res);
  and and_2 (and_2_out, state, not_9_out);
  and and_3 (and_3_out, ~register_2_q, not_10_out);  // AND_Gate
  Adder #(.width(5)) adder_4 (.a(x), .b(multiplexer_1_out), .out(adder_4_out));  // open: cin, cout
  Multiplexer #(.width(5), .enable("false")) multiplexer_1 (
    .in0({5{1'b1}}), .in1(5'b00001), .out(multiplexer_1_out), .sel(xor_1_out));
  Multiplexer #(.width(5), .enable("false")) multiplexer_2 (
    .in0({5{1'b1}}), .in1(5'b00001), .out(multiplexer_2_out), .sel(vy));
  assign controlled_buffer_8_out = and_3_out ? 5'b00011 : 5'bz;  // Controlled_Buffer controlled_buffer_8
  not not_10 (not_10_out, and_1_out);
  assign controlled_buffer_8_out = and_1_out ? adder_4_out : 5'bz;  // Controlled_Buffer controlled_buffer_9
  Adder #(.width(5)) adder_5 (.a(y), .b(multiplexer_2_out), .out(adder_5_out));  // open: cin, cout
  assign controlled_buffer_10_out = and_2_out ? adder_5_out : 5'bz;  // Controlled_Buffer controlled_buffer_10
  not not_11 (not_11_out, and_2_out);
  assign controlled_buffer_10_out = not_11_out ? 5'b01111 : 5'bz;  // Controlled_Buffer controlled_buffer_11
  assign controlled_buffer_8_out = and_4_out ? 5'b11100 : 5'bz;  // Controlled_Buffer controlled_buffer_12
  and and_4 (and_4_out, not_10_out, register_2_q);
  Register #(.width(1)) register_3 (.D(and_1_out), .Q(register_3_q), .clk(_2clk));  // open: en, clr
  Comparator #(.width(5)) comparator_4 (.a(x), .b({5{1'b0}}), .eq(goal2));  // open: gt, lt
  Comparator #(.width(5)) comparator_5 (.a(x), .b({5{1'b1}}), .eq(goal1));  // open: gt, lt
  clllision clllision_1 (.bat(lb), .yball(y), .out_5(clllision_1_out_5), .xball(x), .in(5'b00010));
  clllision clllision_2 (.bat(rb), .yball(y), .out_5(clllision_2_out_5), .xball(x), .in(5'b11101));
  Register #(.width(1)) register_4 (.D(and_2_out), .Q(register_4_q), .clk(_4clk));  // open: en, clr
  Register #(.width(5)) u_x (.D(controlled_buffer_8_out), .en(register_3_q), .Q(x), .clk(_2clk));  // open: clr
  Register #(.width(5)) u_y (.D(controlled_buffer_10_out), .en(register_4_q), .Q(y), .clk(_4clk));  // open: clr
  Pull_Resistor pull_resistor_2 (.node(pull_resistor_2_node));
  assign pull_resistor_2_node = nonstop ? goal2 : 1'bz;  // Controlled_Buffer controlled_buffer_13
  Pull_Resistor pull_resistor_3 (.node(pull_resistor_3_node));
  assign pull_resistor_3_node = nonstop ? goal1 : 1'bz;  // Controlled_Buffer controlled_buffer_14
  Comparator #(.width(5)) comparator_6 (.a(y), .b({5{1'b0}}), .eq(comparator_6_eq));  // open: gt, lt
  Comparator #(.width(5)) comparator_7 (.a(y), .b({5{1'b1}}), .eq(comparator_7_eq));  // open: gt, lt
  or or_6 (or_6_out, pull_resistor_2_node, clllision_1_out_5, pull_resistor_3_node, clllision_2_out_5);
  or or_7 (or_7_out, comparator_6_eq, comparator_7_eq);
  or or_8 (or_8_out, pull_resistor_2_node, clllision_1_out_5);
  assign controlled_buffer_15_out = not_12_out ? ad : 1'bz;  // Controlled_Buffer controlled_buffer_15
  not not_12 (not_12_out, register_3_q);
  assign controlled_buffer_16_out = register_3_q ? comparator_6_eq : 1'bz;  // Controlled_Buffer controlled_buffer_16
  assign controlled_buffer_15_out = register_3_q ? or_7_out : 1'bz;  // Controlled_Buffer controlled_buffer_17
  Register #(.width(1)) u_vx (.D(or_8_out), .en(or_6_out), .Q(vx), .clk(_2clk));  // open: clr
  assign controlled_buffer_16_out = not_12_out ? da : 1'bz;  // Controlled_Buffer controlled_buffer_18
  Register #(.width(1)) u_vy (
    .D(controlled_buffer_16_out), .en(controlled_buffer_15_out), .Q(vy), .clk(_2clk));  // open: clr

  // Other names for the same wires on the sheet: ns = nonstop

  // Notes on the sheet:
  //   Collision
  //   x culc
  //   y culc
  //   x =1 - right
  //   x =0 - left
  //   y =1 - up
  //   y =0 - down
endmodule

module lstep (
  input  clk,
  input  [1:0] move,
  input  rs,
  output [4:0] out_4
);

  wire clock_1_out, comparator_1_gt, not_1_out;
  wire [4:0] adder_1_out, controlled_buffer_1_out, multiplexer_1_out;

  Clock clock_1 (.out(clock_1_out));
  Multiplexer #(.select(2), .width(5), .enable("false")) multiplexer_1 (
    .in0({5{1'b0}}), .in1(5'b00001), .in2({5{1'b1}}), .out(multiplexer_1_out), .sel(move));  // open: in3
  // Probe on controlled_buffer_1_out
  Adder #(.width(5)) adder_1 (.a(multiplexer_1_out), .b(out_4), .out(adder_1_out));  // open: cin, cout
  assign controlled_buffer_1_out = not_1_out ? adder_1_out : 5'bz;  // Controlled_Buffer controlled_buffer_1
  not not_1 (not_1_out, rs);
  assign controlled_buffer_1_out = rs ? 5'b01110 : 5'bz;  // Controlled_Buffer controlled_buffer_2
  Comparator #(.width(5), .mode("unsigned")) comparator_1 (
    .a(5'b11110), .b(controlled_buffer_1_out), .gt(comparator_1_gt));  // open: eq, lt
  // Probe on out_4
  Register #(.width(5)) register_1 (
    .D(controlled_buffer_1_out), .en(comparator_1_gt), .Q(out_4), .clk(clk));  // open: clr
endmodule

module gir (
);

  wire and_2_out, and_3_out, cdm_8_mark5_1_p4, cdm_8_mark5_1_p5, cdm_8_mark5_1_p7, cdm_8_mark5_1_p8,
       cdm_8_mark5_1_p9, cdm_8_mark5_1_p10, cdm_8_mark5_1_p11, cdm_8_mark5_1_p12, cdm_8_mark5_1_p13, clk,
       decoder_1_out0, decoder_1_out1, decoder_2_out0, decoder_2_out1, decoder_2_out2, decoder_2_out3,
       decoder_2_out4, decoder_2_out5, decoder_2_out6, decoder_2_out7, decoder_2_out8, decoder_2_out9,
       decoder_2_out10, decoder_2_out11, decoder_2_out12, decoder_2_out13, decoder_2_out14, decoder_2_out15,
       IAck, IOsel, IRQ, not_1_out, not_2_out, READwrite;
  wire [2:0] vec;
  wire [3:0] IOaddr;
  wire [7:0] cdm_8_mark5_1_p16, cdm_8_mark5_1_p17, IOdat, register_1_q;
  wire [7:4] cdm_8_mark5_1_p15;

  Clock clock_1 (.out(clk));
  // Probe on cdm_8_mark5_1_p5
  // Probe on cdm_8_mark5_1_p4
  // Probe on cdm_8_mark5_1_p8
  // Probe on cdm_8_mark5_1_p7
  // Probe on cdm_8_mark5_1_p10
  // Probe on cdm_8_mark5_1_p9
  and and_1 (IOsel, cdm_8_mark5_1_p15[4], cdm_8_mark5_1_p15[5], cdm_8_mark5_1_p15[6], cdm_8_mark5_1_p15[7], decoder_1_out1);
  // Probe on cdm_8_mark5_1_p11
  Decoder #(.disabled(0)) decoder_1 (
    .out0(decoder_1_out0), .out1(decoder_1_out1), .sel(cdm_8_mark5_1_p12), .en(cdm_8_mark5_1_p13));
  // CdM_8_mark5 cdm_8_mark5_1: pin names not known; wires that end beside it: IRQ, vec, IAck, cdm_8_mark5_1_p4, cdm_8_mark5_1_p5, clk, cdm_8_mark5_1_p7, cdm_8_mark5_1_p8, cdm_8_mark5_1_p9, cdm_8_mark5_1_p10, cdm_8_mark5_1_p11, cdm_8_mark5_1_p12, cdm_8_mark5_1_p13, READwrite, {cdm_8_mark5_1_p15, IOaddr}, cdm_8_mark5_1_p16, cdm_8_mark5_1_p17
  not not_1 (not_1_out, READwrite);
  assign IOdat = not_1_out ? cdm_8_mark5_1_p16 : 8'bz;  // Controlled_Buffer controlled_buffer_1
  assign cdm_8_mark5_1_p17 = READwrite ? IOdat : 8'bz;  // Controlled_Buffer controlled_buffer_2
  and and_2 (and_2_out, decoder_1_out1, ~IOsel);  // AND_Gate
  // Probe on {cdm_8_mark5_1_p15, IOaddr}
  not not_2 (not_2_out, clk);
  // Probe on IOdat
  RAM ram_1 (
    .addr({cdm_8_mark5_1_p15, IOaddr}), .data(IOdat), .sel(and_2_out), .clk(not_2_out), .ld(READwrite));  // open: clr
  ROM rom_1 (.addr({cdm_8_mark5_1_p15, IOaddr}), .data(IOdat), .sel(decoder_1_out0));
  and and_3 (and_3_out, IOsel, IOaddr[0], ~IOaddr[1], ~IOaddr[2], ~IOaddr[3]);  // AND_Gate
  Decoder #(.select(4), .enable("false")) decoder_2 (
    .out0(decoder_2_out0), .out1(decoder_2_out1), .out2(decoder_2_out2), .out3(decoder_2_out3),
    .out4(decoder_2_out4), .out5(decoder_2_out5), .out6(decoder_2_out6), .out7(decoder_2_out7),
    .out8(decoder_2_out8), .out9(decoder_2_out9), .out10(decoder_2_out10), .out11(decoder_2_out11),
    .out12(decoder_2_out12), .out13(decoder_2_out13), .out14(decoder_2_out14), .out15(decoder_2_out15),
    .sel(register_1_q[3:0]));
  Register register_1 (.D(IOdat), .en(and_3_out), .Q(register_1_q), .clk(clk));  // open: clr
  DotMatrix #(.inputtype("row"), .matrixcols(1), .matrixrows(1)) dotmatrix_1 (.row0(decoder_2_out0));
  DotMatrix #(.inputtype("row"), .matrixcols(1), .matrixrows(1)) dotmatrix_2 (.row0(decoder_2_out1));
  DotMatrix #(.inputtype("row"), .matrixcols(1), .matrixrows(1)) dotmatrix_3 (.row0(decoder_2_out2));
  DotMatrix #(.inputtype("row"), .matrixcols(1), .matrixrows(1)) dotmatrix_4 (.row0(decoder_2_out3));
  DotMatrix #(.inputtype("row"), .matrixcols(1), .matrixrows(1)) dotmatrix_5 (.row0(decoder_2_out4));
  DotMatrix #(.inputtype("row"), .matrixcols(1), .matrixrows(1)) dotmatrix_6 (.row0(decoder_2_out5));
  DotMatrix #(.inputtype("row"), .matrixcols(1), .matrixrows(1)) dotmatrix_7 (.row0(decoder_2_out6));
  DotMatrix #(.inputtype("row"), .matrixcols(1), .matrixrows(1)) dotmatrix_8 (.row0(decoder_2_out7));
  DotMatrix #(.inputtype("row"), .matrixcols(1), .matrixrows(1)) dotmatrix_9 (.row0(decoder_2_out8));
  DotMatrix #(.inputtype("row"), .matrixcols(1), .matrixrows(1)) dotmatrix_10 (.row0(decoder_2_out9));
  DotMatrix #(.inputtype("row"), .matrixcols(1), .matrixrows(1)) dotmatrix_11 (.row0(decoder_2_out10));
  DotMatrix #(.inputtype("row"), .matrixcols(1), .matrixrows(1)) dotmatrix_12 (.row0(decoder_2_out11));
  DotMatrix #(.inputtype("row"), .matrixcols(1), .matrixrows(1)) dotmatrix_13 (.row0(decoder_2_out12));
  DotMatrix #(.inputtype("row"), .matrixcols(1), .matrixrows(1)) dotmatrix_14 (.row0(decoder_2_out13));
  DotMatrix #(.inputtype("row"), .matrixcols(1), .matrixrows(1)) dotmatrix_15 (.row0(decoder_2_out14));
  DotMatrix #(.inputtype("row"), .matrixcols(1), .matrixrows(1)) dotmatrix_16 (.row0(decoder_2_out15));

  // Notes on the sheet:
  //   contents of rom_1 (hex, n*v repeats v):
  //   cd f0 d1 f d3 f1 76 ec d d2 0 ee e 8e ae ee 6 d4
endmodule

module xball (
  input  clk,
  input  state,
  input  vx,
  output [4:0] out_4
);

  wire not_1_out, not_2_out;
  wire [4:0] adder_1_out, multiplexer_1_out, register_1_q;

  not not_1 (not_1_out, state);
  Adder #(.width(5)) adder_1 (.a(register_1_q), .b(multiplexer_1_out), .out(adder_1_out));  // open: cin, cout
  Multiplexer #(.width(5), .enable("false")) multiplexer_1 (
    .in0(5'b11110), .in1(5'b00010), .out(multiplexer_1_out), .sel(vx));
  Register #(.width(5)) register_1 (.D(adder_1_out), .en(not_1_out), .Q(register_1_q), .clk(clk));  // open: clr
  assign out_4 = not_1_out ? register_1_q : 5'bz;  // Controlled_Buffer controlled_buffer_1
  not not_2 (not_2_out, not_1_out);
  assign out_4 = not_2_out ? 5'b01001 : 5'bz;  // Controlled_Buffer controlled_buffer_2
endmodule

module clllision (
  input  [4:0] bat,
  input  [4:0] yball,
  input  [4:0] in,
  input  [4:0] xball,
  output out_5
);

  wire comparator_1_eq, comparator_2_eq, comparator_3_eq, comparator_4_eq, or_1_out;
  wire [4:0] adder_1_out, adder_2_out;

  Adder #(.width(5)) adder_1 (.a(5'b00001), .b(bat), .out(adder_1_out));  // open: cin, cout
  Adder #(.width(5)) adder_2 (.a(bat), .b(5'b00010), .out(adder_2_out));  // open: cin, cout
  Comparator #(.width(5)) comparator_1 (.a(adder_1_out), .b(yball), .eq(comparator_1_eq));  // open: gt, lt
  Comparator #(.width(5)) comparator_2 (.a(bat), .b(yball), .eq(comparator_2_eq));  // open: gt, lt
  Comparator #(.width(5)) comparator_3 (.a(adder_2_out), .b(yball), .eq(comparator_3_eq));  // open: gt, lt
  Comparator #(.width(5)) comparator_4 (.a(in), .b(xball), .eq(comparator_4_eq));  // open: gt, lt
  or or_1 (or_1_out, comparator_1_eq, comparator_2_eq, comparator_3_eq);
  and and_1 (out_5, or_1_out, comparator_4_eq);
endmodule

module rstep (
  input  [6:0] in_1,
  input  clk,
  input  rs,
  output [4:0] out_4
);

  wire clock_1_out, comparator_3_gt, not_1_out;
  wire [1:0] comparator_1_eq;
  wire [4:0] adder_1_out, controlled_buffer_1_out, multiplexer_1_out;

  Comparator #(.width(7)) comparator_1 (.a(in_1), .b(7'b0111000), .eq(comparator_1_eq[0]));  // open: gt, lt
  Comparator #(.width(7)) comparator_2 (.a(in_1), .b(7'b0110010), .eq(comparator_1_eq[1]));  // open: gt, lt
  Clock clock_1 (.out(clock_1_out));
  Multiplexer #(.select(2), .width(5), .enable("false")) multiplexer_1 (
    .in0({5{1'b0}}), .in1(5'b00001), .in2({5{1'b1}}), .out(multiplexer_1_out), .sel(comparator_1_eq));  // open: in3
  // Probe on controlled_buffer_1_out
  assign controlled_buffer_1_out = not_1_out ? adder_1_out : 5'bz;  // Controlled_Buffer controlled_buffer_1
  Adder #(.width(5)) adder_1 (.a(multiplexer_1_out), .b(out_4), .out(adder_1_out));  // open: cin, cout
  not not_1 (not_1_out, rs);
  Comparator #(.width(5), .mode("unsigned")) comparator_3 (
    .a(5'b11110), .b(controlled_buffer_1_out), .gt(comparator_3_gt));  // open: eq, lt
  Register #(.width(5)) register_1 (
    .D(controlled_buffer_1_out), .en(comparator_3_gt), .Q(out_4), .clk(clk));  // open: clr
  assign controlled_buffer_1_out = rs ? 5'b01110 : 5'bz;  // Controlled_Buffer controlled_buffer_2
  // Probe on out_4

  // Notes on the sheet:
  //   ascii 8
  //   ascii 2
  //   UP
  //   DOWN
endmodule

module color (
  input  [4:0] xball,
  input  [2:0] mode,
  input  clk,
  output [31:0] out_4
);

  wire _4clk, _8clk, and_1_out, and_2_out, and_3_out, and_4_out, comparator_1_eq, d_ff_1_q, d_ff_2_q,
       d_ff_3_q, not_2_out, undriven;
  wire [1:0] adder_1_out, register_1_q;
  wire [2:0] adder_2_out, register_2_q;
  wire [3:0] decoder_2_out3;
  wire [4:2] decoder_3_out2;
  wire [31:0] decoder_1_out0;
  wire [31:25] or_1_out;

  not not_1 (_4clk, d_ff_1_q);
  D_Flip_Flop d_ff_1 (.clk(clk), .D(_4clk), .Q(d_ff_1_q));  // open: Qn, preset, en, reset
  D_Flip_Flop d_ff_2 (.clk(_4clk), .D(not_2_out), .Q(d_ff_2_q));  // open: Qn, preset, en, reset
  not not_2 (not_2_out, d_ff_2_q);
  D_Flip_Flop d_ff_3 (.clk(not_2_out), .D(_8clk), .Q(d_ff_3_q));  // open: Qn, preset, en, reset
  Decoder #(.select(5)) decoder_1 (
    .out0(decoder_1_out0[0]), .out1(decoder_1_out0[1]), .out2(decoder_1_out0[2]), .out3(decoder_1_out0[3]),
    .out4(decoder_1_out0[4]), .out5(decoder_1_out0[5]), .out6(decoder_1_out0[6]), .out7(decoder_1_out0[7]),
    .out8(decoder_1_out0[8]), .out9(decoder_1_out0[9]), .out10(decoder_1_out0[10]),
    .out11(decoder_1_out0[11]), .out12(decoder_1_out0[12]), .out13(decoder_1_out0[13]),
    .out14(decoder_1_out0[14]), .out15(decoder_1_out0[15]), .out16(decoder_1_out0[16]),
    .out17(decoder_1_out0[17]), .out18(decoder_1_out0[18]), .out19(decoder_1_out0[19]),
    .out20(decoder_1_out0[20]), .out21(decoder_1_out0[21]), .out22(decoder_1_out0[22]),
    .out23(decoder_1_out0[23]), .out24(decoder_1_out0[24]), .out25(decoder_1_out0[25]),
    .out26(decoder_1_out0[26]), .out27(decoder_1_out0[27]), .out28(decoder_1_out0[28]),
    .out29(decoder_1_out0[29]), .out30(decoder_1_out0[30]), .out31(decoder_1_out0[31]), .sel(xball),
    .en(and_1_out));
  and and_1 (and_1_out, ~mode[2], ~mode[1], ~mode[0]);  // AND_Gate
  not not_3 (_8clk, d_ff_3_q);
  assign out_4 = and_1_out ? decoder_1_out0 : 32'bz;  // Controlled_Buffer controlled_buffer_1
  and and_2 (and_2_out, mode[0], ~mode[1], ~mode[2]);  // AND_Gate
  Adder #(.width(2)) adder_1 (.a(register_1_q), .b(2'b01), .out(adder_1_out));  // open: cin, cout
  and and_3 (and_3_out, ~mode[0], mode[1], ~mode[2]);  // AND_Gate
  Register #(.width(2)) register_1 (.D(adder_1_out), .Q(register_1_q), .clk(_8clk), .clr(undriven));  // open: en
  Decoder #(.select(2), .enable("false")) decoder_2 (
    .out0(decoder_2_out3[0]), .out1(decoder_2_out3[1]), .out2(decoder_2_out3[2]), .out3(decoder_2_out3[3]),
    .sel(register_1_q));
  assign out_4 = and_2_out ? {decoder_2_out3, decoder_2_out3, decoder_2_out3, decoder_2_out3, decoder_2_out3[0], decoder_2_out3[1], decoder_2_out3[2], decoder_2_out3[3], decoder_2_out3[0], decoder_2_out3[1], decoder_2_out3[2], decoder_2_out3[3], decoder_2_out3[0], decoder_2_out3[1], decoder_2_out3[2], decoder_2_out3[3], decoder_2_out3[0], decoder_2_out3[1], decoder_2_out3[2], decoder_2_out3[3]} : 32'bz;  // Controlled_Buffer controlled_buffer_2
  assign out_4 = and_3_out ? {decoder_2_out3[0], decoder_2_out3[1], decoder_2_out3[2], decoder_2_out3[3], decoder_2_out3[0], decoder_2_out3[1], decoder_2_out3[2], decoder_2_out3[3], decoder_2_out3[0], decoder_2_out3[1], decoder_2_out3[2], decoder_2_out3[3], decoder_2_out3[0], decoder_2_out3[1], decoder_2_out3[2], {2{decoder_2_out3[3]}}, decoder_2_out3[2:0], decoder_2_out3, decoder_2_out3, decoder_2_out3} : 32'bz;  // Controlled_Buffer controlled_buffer_3
  and and_4 (and_4_out, mode[0], mode[1], ~mode[2]);  // AND_Gate
  assign out_4 = and_4_out ? {or_1_out, or_1_out[29:25], or_1_out[29:25], or_1_out[29:25], or_1_out[29:25], or_1_out[29:25]} : 32'bz;  // Controlled_Buffer controlled_buffer_4
  Adder #(.width(3)) adder_2 (.a(register_2_q), .b(3'b001), .out(adder_2_out));  // open: cin, cout
  Comparator #(.width(3)) comparator_1 (.a(3'b101), .b(register_2_q), .eq(comparator_1_eq));  // open: gt, lt
  Register #(.width(3)) register_2 (.D(adder_2_out), .Q(register_2_q), .clk(_4clk), .clr(comparator_1_eq));  // open: en
  Decoder #(.select(3), .enable("false")) decoder_3 (
    .out0(or_1_out[30]), .out1(or_1_out[31]), .out2(decoder_3_out2[2]), .out3(decoder_3_out2[3]),
    .out4(decoder_3_out2[4]), .sel(register_2_q));  // open: out5, out6, out7
  assign or_1_out[29:25] = {decoder_3_out2, or_1_out[31:30]} | {or_1_out[30], decoder_3_out2, or_1_out[31]};  // OR_Gate or_1, 5 bits wide
endmodule

module screen (
  input  [2:0] state,
  input  [4:0] ballx,
  input  [4:0] bally,
  input  [4:0] left_bat,
  input  [4:0] right_bat,
  output [31:0] out_6,
  output [31:0] out_7,
  output [31:0] out_8,
  output [31:0] out_9,
  output [31:0] out_10,
  output [31:0] out_11,
  output [31:0] out_12,
  output [31:0] out_13,
  output [31:0] out_14,
  output [31:0] out_15,
  output [31:0] out_16,
  output [31:0] out_17,
  output [31:0] out_18,
  output [31:0] out_19,
  output [31:0] out_20,
  output [31:0] out_21,
  output [31:0] out_22,
  output [31:0] out_23,
  output [31:0] out_24,
  output [31:0] out_25,
  output [31:0] out_26,
  output [31:0] out_27,
  output [31:0] out_28,
  output [31:0] out_29,
  output [31:0] out_30,
  output [31:0] out_31,
  output [31:0] out_32,
  output [31:0] out_33,
  output [31:0] out_34,
  output [31:0] out_35,
  output [31:0] out_36,
  output [31:0] out_37
);

  wire and_1_out;
  wire [4:0] n8rows_1_out_14, n8rows_1_out_15, n8rows_1_out_16, n8rows_1_out_17, n8rows_1_out_18,
       n8rows_2_out_14, n8rows_2_out_15, n8rows_2_out_16, n8rows_2_out_17, n8rows_2_out_18, n8rows_3_out_14,
       n8rows_3_out_15, n8rows_3_out_16, n8rows_3_out_17, n8rows_3_out_18;
  wire [31:0] n8rows_1_out_6, n8rows_1_out_7, n8rows_1_out_8, n8rows_1_out_9, n8rows_1_out_10,
       n8rows_1_out_11, n8rows_1_out_12, n8rows_1_out_13, n8rows_2_out_6, n8rows_2_out_7, n8rows_2_out_8,
       n8rows_2_out_9, n8rows_2_out_10, n8rows_2_out_11, n8rows_2_out_12, n8rows_2_out_13, n8rows_3_out_6,
       n8rows_3_out_7, n8rows_3_out_8, n8rows_3_out_9, n8rows_3_out_10, n8rows_3_out_11, n8rows_3_out_12,
       n8rows_3_out_13, n8rows_4_out_6, n8rows_4_out_7, n8rows_4_out_8, n8rows_4_out_9, n8rows_4_out_10,
       n8rows_4_out_11, n8rows_4_out_12, n8rows_4_out_13;

  and and_1 (and_1_out, ~state[0], ~state[1], ~state[2]);  // AND_Gate
  assign out_23 = 1'b1 ? n8rows_1_out_12 : 32'bz;  // Controlled_Buffer controlled_buffer_1
  assign out_35 = 1'b1 ? n8rows_1_out_6 : 32'bz;  // Controlled_Buffer controlled_buffer_2
  assign out_29 = 1'b1 ? n8rows_1_out_9 : 32'bz;  // Controlled_Buffer controlled_buffer_3
  assign out_8 = 1'b1 ? n8rows_2_out_7 : 32'bz;  // Controlled_Buffer controlled_buffer_4
  assign out_11 = 1'b1 ? n8rows_2_out_10 : 32'bz;  // Controlled_Buffer controlled_buffer_5
  assign out_20 = 1'b1 ? n8rows_3_out_11 : 32'bz;  // Controlled_Buffer controlled_buffer_6
  assign out_17 = 1'b1 ? n8rows_3_out_8 : 32'bz;  // Controlled_Buffer controlled_buffer_7
  assign out_14 = 1'b1 ? n8rows_2_out_13 : 32'bz;  // Controlled_Buffer controlled_buffer_8
  assign out_24 = 1'b1 ? n8rows_4_out_6 : 32'bz;  // Controlled_Buffer controlled_buffer_9
  assign out_36 = 1'b1 ? n8rows_4_out_12 : 32'bz;  // Controlled_Buffer controlled_buffer_10
  assign out_30 = 1'b1 ? n8rows_4_out_9 : 32'bz;  // Controlled_Buffer controlled_buffer_11
  assign out_25 = 1'b1 ? n8rows_1_out_11 : 32'bz;  // Controlled_Buffer controlled_buffer_12
  assign out_31 = 1'b1 ? n8rows_1_out_8 : 32'bz;  // Controlled_Buffer controlled_buffer_13
  _8rows u_8rows_1 (
    .in_1({5{1'b0}}), .in_2(ballx), .in_3(bally), .in_4(left_bat), .in_5(right_bat), .out_6(n8rows_1_out_6),
    .out_7(n8rows_1_out_7), .out_8(n8rows_1_out_8), .out_9(n8rows_1_out_9), .out_10(n8rows_1_out_10),
    .out_11(n8rows_1_out_11), .out_12(n8rows_1_out_12), .out_13(n8rows_1_out_13), .out_14(n8rows_1_out_14),
    .out_15(n8rows_1_out_15), .out_16(n8rows_1_out_16), .out_17(n8rows_1_out_17), .out_18(n8rows_1_out_18));
  assign out_7 = 1'b1 ? n8rows_2_out_6 : 32'bz;  // Controlled_Buffer controlled_buffer_14
  assign out_10 = 1'b1 ? n8rows_2_out_9 : 32'bz;  // Controlled_Buffer controlled_buffer_15
  assign out_13 = 1'b1 ? n8rows_2_out_12 : 32'bz;  // Controlled_Buffer controlled_buffer_16
  _8rows u_8rows_2 (
    .in_1(n8rows_1_out_14), .in_2(n8rows_1_out_15), .in_3(n8rows_1_out_16), .in_4(n8rows_1_out_17),
    .in_5(n8rows_1_out_18), .out_6(n8rows_2_out_6), .out_7(n8rows_2_out_7), .out_8(n8rows_2_out_8),
    .out_9(n8rows_2_out_9), .out_10(n8rows_2_out_10), .out_11(n8rows_2_out_11), .out_12(n8rows_2_out_12),
    .out_13(n8rows_2_out_13), .out_14(n8rows_2_out_14), .out_15(n8rows_2_out_15), .out_16(n8rows_2_out_16),
    .out_17(n8rows_2_out_17), .out_18(n8rows_2_out_18));
  assign out_22 = 1'b1 ? n8rows_3_out_13 : 32'bz;  // Controlled_Buffer controlled_buffer_17
  assign out_19 = 1'b1 ? n8rows_3_out_10 : 32'bz;  // Controlled_Buffer controlled_buffer_18
  assign out_16 = 1'b1 ? n8rows_3_out_7 : 32'bz;  // Controlled_Buffer controlled_buffer_19
  _8rows u_8rows_3 (
    .in_1(n8rows_2_out_14), .in_2(n8rows_2_out_15), .in_3(n8rows_2_out_16), .in_4(n8rows_2_out_17),
    .in_5(n8rows_2_out_18), .out_6(n8rows_3_out_6), .out_7(n8rows_3_out_7), .out_8(n8rows_3_out_8),
    .out_9(n8rows_3_out_9), .out_10(n8rows_3_out_10), .out_11(n8rows_3_out_11), .out_12(n8rows_3_out_12),
    .out_13(n8rows_3_out_13), .out_14(n8rows_3_out_14), .out_15(n8rows_3_out_15), .out_16(n8rows_3_out_16),
    .out_17(n8rows_3_out_17), .out_18(n8rows_3_out_18));
  assign out_28 = 1'b1 ? n8rows_4_out_8 : 32'bz;  // Controlled_Buffer controlled_buffer_20
  assign out_34 = 1'b1 ? n8rows_4_out_11 : 32'bz;  // Controlled_Buffer controlled_buffer_21
  _8rows u_8rows_4 (
    .in_1(n8rows_3_out_14), .in_2(n8rows_3_out_15), .in_3(n8rows_3_out_16), .in_4(n8rows_3_out_17),
    .in_5(n8rows_3_out_18), .out_6(n8rows_4_out_6), .out_7(n8rows_4_out_7), .out_8(n8rows_4_out_8),
    .out_9(n8rows_4_out_9), .out_10(n8rows_4_out_10), .out_11(n8rows_4_out_11), .out_12(n8rows_4_out_12),
    .out_13(n8rows_4_out_13));  // open: out_14, out_15, out_16, out_17, out_18
  assign out_27 = 1'b1 ? n8rows_1_out_10 : 32'bz;  // Controlled_Buffer controlled_buffer_22
  assign out_33 = 1'b1 ? n8rows_1_out_7 : 32'bz;  // Controlled_Buffer controlled_buffer_23
  assign out_6 = 1'b1 ? n8rows_1_out_13 : 32'bz;  // Controlled_Buffer controlled_buffer_24
  assign out_15 = 1'b1 ? n8rows_3_out_6 : 32'bz;  // Controlled_Buffer controlled_buffer_25
  assign out_12 = 1'b1 ? n8rows_2_out_11 : 32'bz;  // Controlled_Buffer controlled_buffer_26
  assign out_9 = 1'b1 ? n8rows_2_out_8 : 32'bz;  // Controlled_Buffer controlled_buffer_27
  assign out_21 = 1'b1 ? n8rows_3_out_12 : 32'bz;  // Controlled_Buffer controlled_buffer_28
  assign out_18 = 1'b1 ? n8rows_3_out_9 : 32'bz;  // Controlled_Buffer controlled_buffer_29
  assign out_26 = 1'b1 ? n8rows_4_out_7 : 32'bz;  // Controlled_Buffer controlled_buffer_30
  assign out_32 = 1'b1 ? n8rows_4_out_10 : 32'bz;  // Controlled_Buffer controlled_buffer_31
  assign out_37 = 1'b1 ? n8rows_4_out_13 : 32'bz;  // Controlled_Buffer controlled_buffer_32

  // Other names for the same wires on the sheet: port1[31:0] = out_35; port2[31:0] = out_33; port3[31:0] = out_31;
  //   port4[31:0] = out_29; port5[31:0] = out_27; port6[31:0] = out_25; port7[31:0] = out_23; port8[31:0] = out_6;
  //   port9[31:0] = out_7; port10[31:0] = out_8; port11[31:0] = out_9; port12[31:0] = out_10; port13[31:0] = out_11;
  //   port14[31:0] = out_12; port15[31:0] = out_13; port16[31:0] = out_14; port17[31:0] = out_15;
  //   port18[31:0] = out_16; port19[31:0] = out_17; port20[31:0] = out_18; port21[31:0] = out_19;
  //   port22[31:0] = out_20; port23[31:0] = out_21; port24[31:0] = out_22; port25[31:0] = out_24;
  //   port26[31:0] = out_26; port27[31:0] = out_28; port28[31:0] = out_30; port29[31:0] = out_32;
  //   port30[31:0] = out_34; port31[31:0] = out_36; port32[31:0] = out_37
endmodule
